# Fritzing sketch ArduinoUnoPrototype (saved by Fritzing 0.9.10b)

parts:
  Bauteil2 = Arduino Uno (Rev3) - ICSP
  Bauteil3 = LCD Keypad Shield
  Bauteil4 = Adafruit Proto Shield for Arduino Kit - v.5
  Q1 = NPN-Transistor [package="TO92 [THT]"]
  R1 = Trimmer Potentiometer [maximum_resistance=300kΩ knob_status=50% power=0.5W package=THT]

nets:
  N1: Bauteil2.A1, Bauteil4.A4, Bauteil4.1#183, Bauteil4.P$5#184, Q1.C
  GND: Bauteil2.GND, Bauteil3.GND, Bauteil4.P$11, Bauteil4.GND, Bauteil4.1#156, Bauteil4.P$5#157, Bauteil4.P$6#158, Bauteil4.N$108, Q1.E, R1.wiper
  N2: Bauteil2.D13/SCK, Bauteil4.D13
  N3: Bauteil2.D2, Bauteil4.D2
  N4: Bauteil2.D3_PWM, Bauteil4.D3
  5V: Bauteil2.5V, Bauteil3.VIN
  N5: Bauteil4.1#163, Bauteil4.P$5#164, Bauteil4.P$6#165, Bauteil4.N$195, Q1.B, R1.leg2
  N6: Bauteil4.N$81, R1.leg1

custom parts:
  LCD Keypad Shield: It consists of a 1602 white character blue backlight LCD. The keypad consists of 5 keys — select, up, right, down and left. To save the digital IO pins, the keypad interface uses only one ADC channel. The key value is read through a 5 stage voltage divider.
  Adafruit Proto Shield for Arduino Kit - v.5: Arduino prototyping shield designed by Adafruit Industries
