# Fritzing sketch Flaschenfueller (saved by Fritzing 0.9.3b)
breadboards: 3

parts:
  U1 = TRANSISTOR_NPN_2 [part_number=IRF540N package=to-92]
  Bauteil1 = Arduino Nano (Rev3.0)
  D1 = Zener Diode [part_number=1N4004 breakdown_voltage=3.6V package="300 mil [THT]"]
  LCD1 = 2.8" SPI TFT Module [part_number=MSP2807]
  R1 = Resistor [tolerance=±5% resistance=10k package="2512 [SMD]"]
  R2 = Resistor [tolerance=±5% resistance=10k package="2512 [SMD]"]
  R3 = Resistor [tolerance=±5% resistance=10k package="2512 [SMD]"]
  R4 = Resistor [tolerance=±5% resistance=10k package="2512 [SMD]"]
  R5 = Resistor [tolerance=±5% resistance=10k package="2512 [SMD]"]
  R6 = Resistor [tolerance=±5% resistance=10k package="2512 [SMD]"]
  R7 = Resistor [tolerance=±5% resistance=10k package="2512 [SMD]"]
  R8 = Resistor [tolerance=±5% resistance=10k package="2512 [SMD]"]
  R9 = Resistor [tolerance=±5% resistance=10k package="2512 [SMD]"]
  R10 = Resistor [tolerance=±5% resistance=1k package="2512 [SMD]"]
  R11 = Resistor [tolerance=±5% resistance=1k package="2512 [SMD]"]
  R12 = Resistor [tolerance=±5% resistance=1k package="2512 [SMD]"]
  U2 = TRANSISTOR_NPN_2 [part_number=2n2222 package=to-92]
  U3 = TRANSISTOR_NPN_2 [part_number=IRF540N package=to-92]
  D2 = Zener Diode [part_number=1N4004 breakdown_voltage=3.6V package="300 mil [THT]"]
  D3 = Zener Diode [part_number=1N4004 breakdown_voltage=3.6V package="300 mil [THT]"]
  U4 = TRANSISTOR_NPN_2 [part_number=IRF540N package=to-92]
  R13 = Resistor [tolerance=±5% resistance=1k package="2512 [SMD]"]
  D4 = Zener Diode [part_number=1N4004 breakdown_voltage=3.6V package="300 mil [THT]"]
  RY1 = srd-05vdc-sl-c
  J1 = Power Jack [package=power_jack_smd]
  RY2 = srd-05vdc-sl-c
  RY3 = srd-05vdc-sl-c
  RY4 = srd-05vdc-sl-c
  R14 = Resistor [tolerance=±5% resistance=100 package="0402 [SMD]"]
  R15 = Resistor [tolerance=±5% resistance=100 package="0402 [SMD]"]
  Q1 = TRANSISTOR_PNP [part_number=BC557 package=to-92]
  R16 = Resistor [tolerance=±5% resistance=100 package="0402 [SMD]"]
  Q2 = TRANSISTOR_PNP [part_number=BC557 package=to-92]
  R17 = Resistor [tolerance=±5% resistance=100 package="0402 [SMD]"]

nets:
  GND: U1.C, Bauteil1.GND, LCD1.pin2, U2.C, U3.C, U4.C, J1.GND, Q1.E, Q2.E
  N1: U1.B, R13.Pin_0
  N2: U1.E, D3.anode
  N3: Bauteil1.D3, R6.Pin_1
  N4: Bauteil1.D4, R7.Pin_1
  N5: Bauteil1.D5, R8.Pin_1
  N6: Bauteil1.D6, LCD1.pin13
  N7: Bauteil1.D7, R9.Pin_1
  N8: Bauteil1.D8, R2.Pin_1
  N9: Bauteil1.D9, R3.Pin_1
  N10: Bauteil1.D10, R1.Pin_1
  N11: Bauteil1.D11/MOSI, R4.Pin_1
  N12: Bauteil1.D12/MISO, LCD1.pin9
  N13: Bauteil1.VIN, D1.cathode, D2.cathode, D3.cathode, D4.cathode, RY1.pin_2, RY1.pin_5, J1.GNDBREAK, RY2.pin_2, RY2.pin_5, RY3.pin_2, RY3.pin_5, RY4.pin_2, RY4.pin_5
  N14: Bauteil1.5V, LCD1.pin1, LCD1.pin8, R14.Pin_0, R15.Pin_0
  N15: Bauteil1.A6, R14.Pin_1, Q1.C
  N16: Bauteil1.A5, R15.Pin_1, Q2.C
  N17: Bauteil1.A4, R11.Pin_1
  N18: Bauteil1.A3, R12.Pin_1
  N19: Bauteil1.A2, R13.Pin_1
  N20: Bauteil1.A1, R10.Pin_1
  N21: Bauteil1.D13/SCK, R5.Pin_1
  N22: D1.anode, U4.E
  N23: LCD1.pin3, R1.Pin_0
  N24: LCD1.pin4, R2.Pin_0
  N25: LCD1.pin5, R3.Pin_0
  N26: LCD1.pin6, R4.Pin_0
  N27: LCD1.pin7, R5.Pin_0
  N28: LCD1.pin10, R6.Pin_0
  N29: LCD1.pin11, R7.Pin_0
  N30: LCD1.pin12, R8.Pin_0
  N31: LCD1.pin14, R9.Pin_0
  N32: R10.Pin_0, U2.B
  N33: R11.Pin_0, U4.B
  N34: R12.Pin_0, U3.B
  N35: U2.E, D4.anode
  N36: U3.E, D2.anode
  N37: Q1.B, R16.Pin_1
  N38: Q2.B, R17.Pin_1

notes:
  2,8" ILI9341
  320x240
  4 wire SPI
  Touch MSP2807
  Logic 3,3V
  Number
  Pin Label
  Description
  1
  VCC
  5V/3.3V power input
  2
  GND
  Ground
  3
  CS
  LCD chip select signal, low level enable
  4
  RESET
  LCD reset signal, low level reset
  5
  DC/RS
  LCD register / data selection signal,
  high level: register, low level: data
  6
  SDI(MOSI)
  SPI bus write data signal
  7
  SCK
  SPI bus clock signal
  8
  LED
  Backlight control, high level lighting,
  if not controlled, connect 3.3V always bright
  9
  SDO(MISO)
  SPI bus read data signal, if you do not need to the read function, you can not connect it
  (The following is the touch screen signal line wiring, if you do not need to touch function or the module itself does not have touch function, you can not connect them)
  10
  T_CLK
  Touch SPI bus clock signal
  11
  T_CS
  Touch screen chip select signal, low level enable
  12
  T_DIN
  Touch SPI bus input
  13
  T_DO
  Touch SPI bus output
  14
  T_IRQ
  Touch screen interrupt signal, low level when touch is detected
  12V
  Bier Kontakt 1
  Bier Kontakt 2
  1. Ventil 12V
  2. Ventil 12V
  3. Ventil 12V
  4. Ventil 12V

custom parts:
  2.8" SPI TFT Module: A generic 2.8 inch LCD TFT 320x240 display with touchscreen and SD card slot. Uses the ILI9341 controller, like the Adafruit displays of this size uses.
